// Logisim project MIPS_Monociclo.circ as structural Verilog: 13 circuits, main circuit main
module main (
  input  Reset,
  input  Manual,
  input  RegDst,
  input  Jump,
  input  Branch,
  input  MemRead,
  input  MemToReg,
  input  ALUop0,
  input  ALUop1,
  input  MemWrite,
  input  ALUsrc,
  input  RegWrite,
  input  ByteOrWord,
  input  PcToReg,
  input  PcToR31,
  input  JumpFromR,
  input  BGEZAL,
  output [5:0] Opcode,
  output [2:0] ALUcontrol,
  output RegDst_2,
  output Jump_2,
  output Branch_2,
  output MemRead_2,
  output MemToReg_2,
  output ALUop0_2,
  output ALUop1_2,
  output MemWrite_2,
  output ALUSrc_2,
  output RegWrite_2,
  output ByteOrWord_2,
  output PcToReg_2,
  output PcToR31_2,
  output JumpFromR_2,
  output BGEZAL_2
);

  wire alu_1_negative, alu_1_zero, and_1_out, and_3_out, and_4_out, Clock_out, not_1_out, not_2_out,
       not_3_out, not_4_out, or_1_out, TypeRControl_typerinstruction;
  wire [0:0] and_2_out;
  wire [4:0] instruction_decode_1__15_11, instruction_decode_1__20_16, instruction_decode_1__25_21,
       multiplexer_2_out, multiplexer_4_out;
  wire [5:0] instruction_decode_1__15_0;
  wire [14:0] rom_1_data, TypeRControl_out_5;
  wire [15:6] instruction_decode_1__15_0_2;
  wire [27:0] adder_1_out;
  wire [31:0] adder_2_out, alu_1_out_8, bit_extender_1_out, memoryout_1_out_4, multiplexer_3_out,
       multiplexer_5_out, multiplexer_6_out, multiplexer_7_out, PC_q, ram_1_data,
       register_bank_1_read_data_1, register_bank_1_read_data_2, rom_2_data, shl_26_28_1_out_2,
       shl_32_1_out_2;

  Clock Clock (.out(Clock_out));
  and and_1 (and_1_out, not_2_out, not_1_out);
  Register #(.width(32)) PC (.D(multiplexer_7_out), .en(1'b1), .Q(PC_q), .clk(Clock_out), .clr(Reset));
  not not_1 (not_1_out, TypeRControl_typerinstruction);
  not not_2 (not_2_out, Manual);
  ROM #(.addrWidth(6), .dataWidth(15)) rom_1 (.addr(Opcode), .data(rom_1_data), .sel(and_1_out));
  Adder #(.width(32)) adder_1 (.a(32'h4), .b(PC_q), .out({shl_26_28_1_out_2[31:28], adder_1_out}));  // open: cin, cout
  ROM #(.addrWidth(24), .dataWidth(32)) rom_2 (.addr(PC_q[25:2]), .data(rom_2_data), .sel(1'b1));
  TypeRControl TypeRControl (
    .opcode(Opcode), .funct(instruction_decode_1__15_0), .Manual(Manual),
    .TypeRInstruction(TypeRControl_typerinstruction), .out_5(TypeRControl_out_5));
  not not_3 (not_3_out, Manual);
  Instruction_Decode instruction_decode_1 (
    .in_1(rom_2_data), ._31_26(Opcode), ._25_21(instruction_decode_1__25_21),
    ._20_16(instruction_decode_1__20_16), ._15_11(instruction_decode_1__15_11),
    ._15_0({instruction_decode_1__15_0_2, instruction_decode_1__15_0}));
  and and_2 (and_2_out[0], not_3_out, TypeRControl_typerinstruction);
  Multiplexer #(.select(2), .width(15), .enable("false")) multiplexer_1 (
    .in0(rom_1_data), .in1(TypeRControl_out_5),
    .in2({BGEZAL, JumpFromR, PcToR31, PcToReg, ByteOrWord, RegWrite, ALUsrc, MemWrite, ALUop1, ALUop0, MemToReg, MemRead, Branch, Jump, RegDst}),
    .out({BGEZAL_2, JumpFromR_2, PcToR31_2, PcToReg_2, ByteOrWord_2, RegWrite_2, ALUSrc_2, MemWrite_2, ALUop1_2, ALUop0_2, MemToReg_2, MemRead_2, Branch_2, Jump_2, RegDst_2}),
    .sel({Manual, and_2_out[0]}));  // open: in3
  shl_26_28 shl_26_28_1 (
    .in_1({instruction_decode_1__25_21, instruction_decode_1__20_16, instruction_decode_1__15_0_2, instruction_decode_1__15_0}),
    .out_2(shl_26_28_1_out_2[27:0]));
  Multiplexer #(.select(2), .width(5), .enable("false")) multiplexer_2 (
    .in0(instruction_decode_1__20_16), .in1(instruction_decode_1__15_11), .in2({5{1'b1}}),
    .out(multiplexer_2_out), .sel({PcToR31_2, RegDst_2}));  // open: in3
  Register_Bank register_bank_1 (
    .Read_1_Address(instruction_decode_1__25_21), .Read_2_Address(instruction_decode_1__20_16),
    .Write_Address(multiplexer_2_out), .Write_Data(multiplexer_6_out), .Enable(RegWrite_2), .Reset(Reset),
    .Clock(Clock_out), .Read_Data_1(register_bank_1_read_data_1), .Read_Data_2(register_bank_1_read_data_2));
  assign bit_extender_1_out = {{16{instruction_decode_1__15_0_2[15]}}, {instruction_decode_1__15_0_2, instruction_decode_1__15_0}};  // Bit_Extender bit_extender_1
  shl_32 shl_32_1 (.in_1(bit_extender_1_out), .out_2(shl_32_1_out_2));
  Multiplexer #(.width(32), .enable("false")) multiplexer_3 (
    .in0(register_bank_1_read_data_2), .in1(bit_extender_1_out), .out(multiplexer_3_out), .sel(ALUSrc_2));
  Adder #(.width(32)) adder_2 (
    .a({shl_26_28_1_out_2[31:28], adder_1_out}), .b(shl_32_1_out_2), .out(adder_2_out));  // open: cin, cout
  ALU alu_1 (
    .in_1(register_bank_1_read_data_1), .in_2(multiplexer_3_out), .in_3(ALUcontrol), .Clock(Clock_out),
    .Reset(Reset), .Zero(alu_1_zero), .out_8(alu_1_out_8), .Negative(alu_1_negative));
  Multiplexer #(.width(5), .enable("false")) multiplexer_4 (
    .in0(instruction_decode_1__15_0[4:0]), .in1(instruction_decode_1__20_16), .out(multiplexer_4_out),
    .sel(PcToReg_2));
  ALU_Control alu_control_1 (.in_1({ALUop1_2, ALUop0_2}), .in_2(multiplexer_4_out), .out_3(ALUcontrol));
  not not_4 (not_4_out, alu_1_negative);
  RAM #(.addrWidth(24), .dataWidth(32), .bus("separate")) ram_1 (
    .addr(alu_1_out_8[25:2]), .din(register_bank_1_read_data_2), .data(ram_1_data), .str(MemWrite_2),
    .sel(1'b1), .clk(Clock_out), .ld(MemRead_2), .clr(1'b0));
  and and_3 (and_3_out, Branch_2, alu_1_zero);
  and and_4 (and_4_out, not_4_out, BGEZAL_2);
  Multiplexer #(.width(32), .enable("false")) multiplexer_5 (
    .in0({shl_26_28_1_out_2[31:28], adder_1_out}), .in1(adder_2_out), .out(multiplexer_5_out), .sel(or_1_out));
  or or_1 (or_1_out, and_3_out, and_4_out);
  MemoryOut memoryout_1 (
    .in_1(ram_1_data), .in_2(alu_1_out_8[1:0]), .ByteOrWord(ByteOrWord_2), .out_4(memoryout_1_out_4));
  Multiplexer #(.select(2), .width(32), .enable("false")) multiplexer_6 (
    .in0(alu_1_out_8), .in1(memoryout_1_out_4), .in2({shl_26_28_1_out_2[31:28], adder_1_out}),
    .out(multiplexer_6_out), .sel({PcToReg_2, MemToReg_2}));  // open: in3
  Multiplexer #(.select(2), .width(32), .enable("false")) multiplexer_7 (
    .in0(multiplexer_5_out), .in1(shl_26_28_1_out_2), .in2(alu_1_out_8), .out(multiplexer_7_out),
    .sel({JumpFromR_2, Jump_2}));  // open: in3

  // Notes on the sheet:
  //   Bloco Operativo
  //   Bloco de Controle
  //   Instruction Memory
  //   contents of rom_1 (hex, n*v repeats v):
  //   241 5a44 2 0 24 9*0 360 17*0 718 0 0 318 7*0 180
  //   contents of rom_2 (hex, n*v repeats v):
  //   8c010000 8c020004 8c030004 8c040008 8c05000c 8c060010 8c070014 8c080018 8c09001c 8c0a0020 8000019
  //   22a020 ac140030 a6a822 ac150034 80b024 ac160038 87b825 ac17003c 39180033 ac180040 124001a 140c809
  //   451fff3 431fff2 1022fffd 1043fffc ac190044 800a0001 ac0a0048
  //   Inst 25-0
  //   Shift Left 2
  //   Registers
  //   Sign Extend
  //   Shift Left 2
  //   ALU
  //   ALU Control
  //   Data Memory
endmodule

module Instruction_Decode (
  input  [31:0] in_1,
  output [5:0] _31_26,
  output [4:0] _25_21,
  output [4:0] _20_16,
  output [4:0] _15_11,
  output [15:0] _15_0
);


  assign _15_0 = in_1[15:0];
  assign _15_11 = in_1[15:11];
  assign _20_16 = in_1[20:16];
  assign _25_21 = in_1[25:21];
  assign _31_26 = in_1[31:26];
endmodule

module Register_Bank (
  input  [4:0] Read_1_Address,
  input  [4:0] Read_2_Address,
  input  [4:0] Write_Address,
  input  [31:0] Write_Data,
  input  Enable,
  input  Reset,
  input  Clock,
  output [31:0] Read_Data_1,
  output [31:0] Read_Data_2
);

  wire and_1_out, and_2_out, and_3_out, and_4_out, and_5_out, and_6_out, and_7_out, and_8_out, and_9_out,
       and_10_out, and_11_out, and_12_out, and_13_out, and_14_out, and_15_out, and_16_out, and_17_out,
       and_18_out, and_19_out, and_20_out, and_21_out, and_22_out, and_23_out, and_24_out, and_25_out,
       and_26_out, and_27_out, and_28_out, and_29_out, and_30_out, and_31_out, and_32_out, dec_5_1_1_out_2,
       dec_5_1_1_out_3, dec_5_1_1_out_4, dec_5_1_1_out_5, dec_5_1_1_out_6, dec_5_1_1_out_7, dec_5_1_1_out_8,
       dec_5_1_1_out_9, dec_5_1_1_out_10, dec_5_1_1_out_11, dec_5_1_1_out_12, dec_5_1_1_out_13,
       dec_5_1_1_out_14, dec_5_1_1_out_15, dec_5_1_1_out_16, dec_5_1_1_out_17, dec_5_1_1_out_18,
       dec_5_1_1_out_19, dec_5_1_1_out_20, dec_5_1_1_out_21, dec_5_1_1_out_22, dec_5_1_1_out_23,
       dec_5_1_1_out_24, dec_5_1_1_out_25, dec_5_1_1_out_26, dec_5_1_1_out_27, dec_5_1_1_out_28,
       dec_5_1_1_out_29, dec_5_1_1_out_30, dec_5_1_1_out_31, dec_5_1_1_out_32, dec_5_1_1_out_33;
  wire [31:0] multiplexer_1_out, multiplexer_2_out, multiplexer_3_out, multiplexer_4_out, register_2_q,
       register_3_q, register_4_q, register_5_q, register_6_q, register_7_q, register_8_q, register_9_q,
       register_10_q, register_11_q, register_12_q, register_13_q, register_14_q, register_15_q,
       register_16_q, register_17_q, register_18_q, register_19_q, register_20_q, register_21_q,
       register_22_q, register_23_q, register_24_q, register_25_q, register_26_q, register_27_q,
       register_28_q, register_29_q, register_30_q, register_31_q, register_32_q;

  Dec_5_1 dec_5_1_1 (
    .in_1(Write_Address), .out_2(dec_5_1_1_out_2), .out_3(dec_5_1_1_out_3), .out_4(dec_5_1_1_out_4),
    .out_5(dec_5_1_1_out_5), .out_6(dec_5_1_1_out_6), .out_7(dec_5_1_1_out_7), .out_8(dec_5_1_1_out_8),
    .out_9(dec_5_1_1_out_9), .out_10(dec_5_1_1_out_10), .out_11(dec_5_1_1_out_11), .out_12(dec_5_1_1_out_12),
    .out_13(dec_5_1_1_out_13), .out_14(dec_5_1_1_out_14), .out_15(dec_5_1_1_out_15),
    .out_16(dec_5_1_1_out_16), .out_17(dec_5_1_1_out_17), .out_18(dec_5_1_1_out_18),
    .out_19(dec_5_1_1_out_19), .out_20(dec_5_1_1_out_20), .out_21(dec_5_1_1_out_21),
    .out_22(dec_5_1_1_out_22), .out_23(dec_5_1_1_out_23), .out_24(dec_5_1_1_out_24),
    .out_25(dec_5_1_1_out_25), .out_26(dec_5_1_1_out_26), .out_27(dec_5_1_1_out_27),
    .out_28(dec_5_1_1_out_28), .out_29(dec_5_1_1_out_29), .out_30(dec_5_1_1_out_30),
    .out_31(dec_5_1_1_out_31), .out_32(dec_5_1_1_out_32), .out_33(dec_5_1_1_out_33));
  and and_1 (and_1_out, dec_5_1_1_out_2, Enable);
  and and_2 (and_2_out, dec_5_1_1_out_3, Enable);
  and and_3 (and_3_out, dec_5_1_1_out_4, Enable);
  and and_4 (and_4_out, dec_5_1_1_out_5, Enable);
  and and_5 (and_5_out, dec_5_1_1_out_6, Enable);
  and and_6 (and_6_out, dec_5_1_1_out_7, Enable);
  and and_7 (and_7_out, dec_5_1_1_out_8, Enable);
  and and_8 (and_8_out, dec_5_1_1_out_9, Enable);
  and and_9 (and_9_out, dec_5_1_1_out_10, Enable);
  and and_10 (and_10_out, dec_5_1_1_out_11, Enable);
  and and_11 (and_11_out, dec_5_1_1_out_12, Enable);
  and and_12 (and_12_out, dec_5_1_1_out_13, Enable);
  and and_13 (and_13_out, dec_5_1_1_out_14, Enable);
  and and_14 (and_14_out, dec_5_1_1_out_15, Enable);
  and and_15 (and_15_out, dec_5_1_1_out_16, Enable);
  and and_16 (and_16_out, dec_5_1_1_out_17, Enable);
  and and_17 (and_17_out, dec_5_1_1_out_18, Enable);
  and and_18 (and_18_out, dec_5_1_1_out_19, Enable);
  and and_19 (and_19_out, dec_5_1_1_out_20, Enable);
  and and_20 (and_20_out, dec_5_1_1_out_21, Enable);
  and and_21 (and_21_out, dec_5_1_1_out_22, Enable);
  and and_22 (and_22_out, dec_5_1_1_out_23, Enable);
  and and_23 (and_23_out, dec_5_1_1_out_24, Enable);
  and and_24 (and_24_out, dec_5_1_1_out_25, Enable);
  and and_25 (and_25_out, dec_5_1_1_out_26, Enable);
  and and_26 (and_26_out, dec_5_1_1_out_27, Enable);
  and and_27 (and_27_out, dec_5_1_1_out_28, Enable);
  and and_28 (and_28_out, dec_5_1_1_out_29, Enable);
  and and_29 (and_29_out, dec_5_1_1_out_30, Enable);
  and and_30 (and_30_out, dec_5_1_1_out_31, Enable);
  and and_31 (and_31_out, dec_5_1_1_out_32, Enable);
  and and_32 (and_32_out, dec_5_1_1_out_33, Enable);
  Register #(.width(32)) register_1 (.D(Write_Data), .en(and_1_out), .clk(Clock), .clr(Reset));  // open: Q
  Register #(.width(32)) register_2 (.D(Write_Data), .en(and_2_out), .Q(register_2_q), .clk(Clock), .clr(Reset));
  Register #(.width(32)) register_3 (.D(Write_Data), .en(and_3_out), .Q(register_3_q), .clk(Clock), .clr(Reset));
  Register #(.width(32)) register_4 (.D(Write_Data), .en(and_4_out), .Q(register_4_q), .clk(Clock), .clr(Reset));
  Register #(.width(32)) register_5 (.D(Write_Data), .en(and_5_out), .Q(register_5_q), .clk(Clock), .clr(Reset));
  Register #(.width(32)) register_6 (.D(Write_Data), .en(and_6_out), .Q(register_6_q), .clk(Clock), .clr(Reset));
  Register #(.width(32)) register_7 (.D(Write_Data), .en(and_7_out), .Q(register_7_q), .clk(Clock), .clr(Reset));
  Register #(.width(32)) register_8 (.D(Write_Data), .en(and_8_out), .Q(register_8_q), .clk(Clock), .clr(Reset));
  Register #(.width(32)) register_9 (.D(Write_Data), .en(and_9_out), .Q(register_9_q), .clk(Clock), .clr(Reset));
  Register #(.width(32)) register_10 (.D(Write_Data), .en(and_10_out), .Q(register_10_q), .clk(Clock), .clr(Reset));
  Register #(.width(32)) register_11 (.D(Write_Data), .en(and_11_out), .Q(register_11_q), .clk(Clock), .clr(Reset));
  Register #(.width(32)) register_12 (.D(Write_Data), .en(and_12_out), .Q(register_12_q), .clk(Clock), .clr(Reset));
  Register #(.width(32)) register_13 (.D(Write_Data), .en(and_13_out), .Q(register_13_q), .clk(Clock), .clr(Reset));
  Register #(.width(32)) register_14 (.D(Write_Data), .en(and_14_out), .Q(register_14_q), .clk(Clock), .clr(Reset));
  Register #(.width(32)) register_15 (.D(Write_Data), .en(and_15_out), .Q(register_15_q), .clk(Clock), .clr(Reset));
  Register #(.width(32)) register_16 (.D(Write_Data), .en(and_16_out), .Q(register_16_q), .clk(Clock), .clr(Reset));
  Register #(.width(32)) register_17 (.D(Write_Data), .en(and_17_out), .Q(register_17_q), .clk(Clock), .clr(Reset));
  Register #(.width(32)) register_18 (.D(Write_Data), .en(and_18_out), .Q(register_18_q), .clk(Clock), .clr(Reset));
  Register #(.width(32)) register_19 (.D(Write_Data), .en(and_19_out), .Q(register_19_q), .clk(Clock), .clr(Reset));
  Register #(.width(32)) register_20 (.D(Write_Data), .en(and_20_out), .Q(register_20_q), .clk(Clock), .clr(Reset));
  Register #(.width(32)) register_21 (.D(Write_Data), .en(and_21_out), .Q(register_21_q), .clk(Clock), .clr(Reset));
  Register #(.width(32)) register_22 (.D(Write_Data), .en(and_22_out), .Q(register_22_q), .clk(Clock), .clr(Reset));
  Register #(.width(32)) register_23 (.D(Write_Data), .en(and_23_out), .Q(register_23_q), .clk(Clock), .clr(Reset));
  Register #(.width(32)) register_24 (.D(Write_Data), .en(and_24_out), .Q(register_24_q), .clk(Clock), .clr(Reset));
  Register #(.width(32)) register_25 (.D(Write_Data), .en(and_25_out), .Q(register_25_q), .clk(Clock), .clr(Reset));
  Register #(.width(32)) register_26 (.D(Write_Data), .en(and_26_out), .Q(register_26_q), .clk(Clock), .clr(Reset));
  Register #(.width(32)) register_27 (.D(Write_Data), .en(and_27_out), .Q(register_27_q), .clk(Clock), .clr(Reset));
  Register #(.width(32)) register_28 (.D(Write_Data), .en(and_28_out), .Q(register_28_q), .clk(Clock), .clr(Reset));
  Register #(.width(32)) register_29 (.D(Write_Data), .en(and_29_out), .Q(register_29_q), .clk(Clock), .clr(Reset));
  Register #(.width(32)) register_30 (.D(Write_Data), .en(and_30_out), .Q(register_30_q), .clk(Clock), .clr(Reset));
  Register #(.width(32)) register_31 (.D(Write_Data), .en(and_31_out), .Q(register_31_q), .clk(Clock), .clr(Reset));
  Register #(.width(32)) register_32 (.D(Write_Data), .en(and_32_out), .Q(register_32_q), .clk(Clock), .clr(Reset));
  Multiplexer #(.select(4), .width(32), .enable("false")) multiplexer_1 (
    .in0({32{1'b0}}), .in1(register_2_q), .in2(register_3_q), .in3(register_4_q), .in4(register_5_q),
    .in5(register_6_q), .in6(register_7_q), .in7(register_8_q), .in8(register_9_q), .in9(register_10_q),
    .in10(register_11_q), .in11(register_12_q), .in12(register_13_q), .in13(register_14_q),
    .in14(register_15_q), .in15(register_16_q), .out(multiplexer_1_out), .sel(Read_2_Address[3:0]));
  Multiplexer #(.select(4), .width(32), .enable("false")) multiplexer_2 (
    .in0({32{1'b0}}), .in1(register_2_q), .in2(register_3_q), .in3(register_4_q), .in4(register_5_q),
    .in5(register_6_q), .in6(register_7_q), .in7(register_8_q), .in8(register_9_q), .in9(register_10_q),
    .in10(register_11_q), .in11(register_12_q), .in12(register_13_q), .in13(register_14_q),
    .in14(register_15_q), .in15(register_16_q), .out(multiplexer_2_out), .sel(Read_1_Address[3:0]));
  Multiplexer #(.select(4), .width(32), .enable("false")) multiplexer_3 (
    .in0(register_17_q), .in1(register_18_q), .in2(register_19_q), .in3(register_20_q), .in4(register_21_q),
    .in5(register_22_q), .in6(register_23_q), .in7(register_24_q), .in8(register_25_q), .in9(register_26_q),
    .in10(register_27_q), .in11(register_28_q), .in12(register_29_q), .in13(register_30_q),
    .in14(register_31_q), .in15(register_32_q), .out(multiplexer_3_out), .sel(Read_1_Address[3:0]));
  Multiplexer #(.select(4), .width(32), .enable("false")) multiplexer_4 (
    .in0(register_17_q), .in1(register_18_q), .in2(register_19_q), .in3(register_20_q), .in4(register_21_q),
    .in5(register_22_q), .in6(register_23_q), .in7(register_24_q), .in8(register_25_q), .in9(register_26_q),
    .in10(register_27_q), .in11(register_28_q), .in12(register_29_q), .in13(register_30_q),
    .in14(register_31_q), .in15(register_32_q), .out(multiplexer_4_out), .sel(Read_2_Address[3:0]));
  Multiplexer #(.width(32), .enable("false")) multiplexer_5 (
    .in0(multiplexer_2_out), .in1(multiplexer_3_out), .out(Read_Data_1), .sel(Read_1_Address[4]));
  Multiplexer #(.width(32), .enable("false")) multiplexer_6 (
    .in0(multiplexer_1_out), .in1(multiplexer_4_out), .out(Read_Data_2), .sel(Read_2_Address[4]));
endmodule

module Dec_5_1 (
  input  [4:0] in_1,
  output out_2,
  output out_3,
  output out_4,
  output out_5,
  output out_6,
  output out_7,
  output out_8,
  output out_9,
  output out_10,
  output out_11,
  output out_12,
  output out_13,
  output out_14,
  output out_15,
  output out_16,
  output out_17,
  output out_18,
  output out_19,
  output out_20,
  output out_21,
  output out_22,
  output out_23,
  output out_24,
  output out_25,
  output out_26,
  output out_27,
  output out_28,
  output out_29,
  output out_30,
  output out_31,
  output out_32,
  output out_33
);

  wire decoder_1_out0, decoder_2_out0, not_1_out, not_2_out, not_3_out, not_4_out;
  wire [3:0] and_1_out, and_5_out;

  not not_1 (not_1_out, in_1[4]);
  not not_2 (not_2_out, in_1[4]);
  not not_3 (not_3_out, in_1[4]);
  not not_4 (not_4_out, in_1[4]);
  and and_1 (and_1_out[0], not_1_out, in_1[0]);
  and and_2 (and_1_out[1], not_2_out, in_1[1]);
  and and_3 (and_1_out[2], not_3_out, in_1[2]);
  and and_4 (and_1_out[3], not_4_out, in_1[3]);
  and and_5 (and_5_out[0], in_1[4], in_1[0]);
  and and_6 (and_5_out[1], in_1[4], in_1[1]);
  and and_7 (and_5_out[2], in_1[4], in_1[2]);
  and and_8 (and_5_out[3], in_1[4], in_1[3]);
  Decoder #(.select(4), .enable("false")) decoder_1 (
    .out0(decoder_1_out0), .out1(out_3), .out2(out_4), .out3(out_5), .out4(out_6), .out5(out_7),
    .out6(out_8), .out7(out_9), .out8(out_10), .out9(out_11), .out10(out_12), .out11(out_13), .out12(out_14),
    .out13(out_15), .out14(out_16), .out15(out_17), .sel(and_1_out));
  Decoder #(.select(4), .enable("false")) decoder_2 (
    .out0(decoder_2_out0), .out1(out_19), .out2(out_20), .out3(out_21), .out4(out_22), .out5(out_23),
    .out6(out_24), .out7(out_25), .out8(out_26), .out9(out_27), .out10(out_28), .out11(out_29),
    .out12(out_30), .out13(out_31), .out14(out_32), .out15(out_33), .sel(and_5_out));
  and and_9 (out_2, not_1_out, decoder_1_out0);
  and and_10 (out_18, in_1[4], decoder_2_out0);
endmodule

module ALU (
  input  [31:0] in_1,
  input  [31:0] in_2,
  input  [2:0] in_3,
  input  Clock,
  input  Reset,
  output Zero,
  output Negative,
  output [31:0] out_8
);

  wire and_2_out, not_1_out, not_2_out, or_2_out, or_3_out, or_4_out, or_5_out, or_6_out;
  wire [31:0] adder_1_out, and_1_out, divider_1_out, divider_1_rem, or_1_out, subtractor_1_out, xor_1_out;

  assign and_1_out = in_1 & in_2;  // AND_Gate and_1, 32 bits wide
  assign or_1_out = in_1 | in_2;  // OR_Gate or_1, 32 bits wide
  Adder #(.width(32)) adder_1 (.a(in_1), .b(in_2), .out(adder_1_out));  // open: cin, cout
  assign xor_1_out = in_1 ^ in_2;  // XOR_Gate xor_1, 32 bits wide
  Subtractor #(.width(32)) subtractor_1 (.a(in_1), .b(in_2), .out(subtractor_1_out));  // open: bin, bout
  Divider #(.width(32)) divider_1 (.a(in_1), .b(in_2), .out(divider_1_out), .rem(divider_1_rem));  // open: upper
  Multiplexer #(.select(3), .width(32), .enable("false")) multiplexer_1 (
    .in0(and_1_out), .in1(or_1_out), .in2(adder_1_out), .in3(in_1), .in4({32{1'b0}}), .in5(xor_1_out),
    .in6(subtractor_1_out), .in7({{31{1'b0}}, subtractor_1_out[31]}), .out({Negative, out_8[30:0]}),
    .sel(in_3));
  not not_1 (not_1_out, in_3[0]);
  not not_2 (not_2_out, in_3[1]);
  and and_2 (and_2_out, not_1_out, not_2_out, in_3[2]);
  Register #(.width(32)) HI (.D(divider_1_rem), .en(and_2_out), .clk(Clock), .clr(Reset));  // open: Q
  Register #(.width(32)) LO (.D(divider_1_out), .en(and_2_out), .clk(Clock), .clr(Reset));  // open: Q
  or or_2 (or_2_out, out_8[0], out_8[1], out_8[2], out_8[3], out_8[4], out_8[5], out_8[6], out_8[7], out_8[8]);
  or or_3 (or_3_out, out_8[9], out_8[10], out_8[11], out_8[12], out_8[13], out_8[14], out_8[15], out_8[16], out_8[17]);
  or or_4 (or_4_out, out_8[18], out_8[19], out_8[20], out_8[21], out_8[22], out_8[23], out_8[24], out_8[25], out_8[26]);
  or or_5 (or_5_out, out_8[27], out_8[28], out_8[29], out_8[30], Negative);
  or or_6 (or_6_out, or_2_out, or_3_out, or_4_out, or_5_out);
  not not_3 (Zero, or_6_out);

  assign out_8[31] = Negative;
endmodule

module shl_26_28 (
  input  [25:0] in_1,
  output [27:0] out_2
);


  assign out_2 = {in_1, 2'b00};
endmodule

module merge_PC (
  input  [27:0] in_1,
  input  [3:0] in_2,
  output [31:0] out_3
);


  assign out_3 = {in_2, in_1};
endmodule

module sig_ext (
  input  [15:0] in_1,
  output [31:0] out_2
);


  assign out_2 = {{17{in_1[15]}}, in_1[14:0]};
endmodule

module shl_32 (
  input  [31:0] in_1,
  output [31:0] out_2
);


  assign out_2 = {in_1[29:0], 2'b00};
endmodule

module ALU_Control (
  input  [1:0] in_1,
  input  [4:0] in_2,
  output [2:0] out_3
);

  wire and_1_out, and_2_out, and_3_out, and_4_out, and_5_out, and_6_out, and_7_out, and_8_out, and_9_out,
       and_10_out, and_11_out, not_1_out, not_2_out, not_3_out, not_4_out, not_5_out, not_6_out, not_7_out;

  not not_1 (not_1_out, in_1[1]);
  not not_2 (not_2_out, in_1[0]);
  not not_3 (not_3_out, in_2[4]);
  not not_4 (not_4_out, in_2[3]);
  not not_5 (not_5_out, in_2[2]);
  not not_6 (not_6_out, in_2[1]);
  not not_7 (not_7_out, in_2[0]);
  and and_1 (and_1_out, in_1[1], not_3_out, not_5_out, in_2[1], not_7_out);
  and and_2 (and_2_out, in_1[1], in_2[3], not_5_out, in_2[1], not_7_out);
  and and_3 (and_3_out, not_2_out, not_3_out, not_4_out, not_5_out, not_7_out);
  and and_4 (and_4_out, not_2_out, not_3_out, in_2[3], not_5_out, not_6_out, in_2[0]);
  and and_5 (and_5_out, not_2_out, not_3_out, not_5_out, in_2[1], not_7_out);
  and and_6 (and_6_out, not_2_out, in_2[4], not_4_out, not_5_out, not_6_out, in_2[0]);
  and and_7 (and_7_out, in_1[1], not_3_out, not_4_out, in_2[2], not_6_out, in_2[0]);
  and and_8 (and_8_out, in_1[1], not_3_out, in_2[3], not_5_out, not_6_out, in_2[0]);
  and and_9 (and_9_out, in_1[1], not_3_out, in_2[3], not_5_out, in_2[1], not_7_out);
  and and_10 (and_10_out, in_1[1], in_2[4], not_4_out, not_5_out, not_6_out, in_2[0]);
  and and_11 (and_11_out, in_1[1], in_1[0]);
  or or_1 (out_3[2], in_1[0], and_1_out, and_2_out);
  or or_2 (out_3[1], not_1_out, and_3_out, and_4_out, and_5_out, and_6_out);
  or or_3 (out_3[0], and_7_out, and_8_out, and_9_out, and_10_out, and_11_out);

  // Notes on the sheet:
  //   b
  //   a
  //   c
  //   d
  //   e
  //   f
  //   g
endmodule

module Debug_Register_Bank (
  input  Debug,
  input  Debug_Enable,
  input  [4:0] Debug_Write_Address,
  input  [31:0] Debug_Write_Data,
  input  [4:0] Read_1_Address,
  input  [4:0] Read_2_Address,
  input  [4:0] Write_Address,
  input  [31:0] Write_Data,
  input  Enable,
  input  Reset,
  input  Clock,
  output [31:0] Read_Data_1,
  output [31:0] Read_Data_2
);

  wire and_1_out, not_1_out, or_1_out;
  wire [4:0] multiplexer_1_out;
  wire [31:0] multiplexer_2_out;

  not not_1 (not_1_out, Debug);
  Multiplexer #(.width(5), .enable("false")) multiplexer_1 (
    .in0(Write_Address), .in1(Debug_Write_Address), .out(multiplexer_1_out), .sel(Debug));
  Multiplexer #(.width(32), .enable("false")) multiplexer_2 (
    .in0(Write_Data), .in1(Debug_Write_Data), .out(multiplexer_2_out), .sel(Debug));
  or or_1 (or_1_out, Debug_Enable, Enable);
  and and_1 (and_1_out, not_1_out, Reset);
  Register_Bank register_bank_1 (
    .Read_1_Address(Read_1_Address), .Read_2_Address(Read_2_Address), .Write_Address(multiplexer_1_out),
    .Write_Data(multiplexer_2_out), .Enable(or_1_out), .Reset(and_1_out), .Clock(Clock),
    .Read_Data_1(Read_Data_1), .Read_Data_2(Read_Data_2));
endmodule

module MemoryOut (
  input  [31:0] in_1,
  input  [1:0] in_2,
  input  ByteOrWord,
  output [31:0] out_4
);

  wire [7:0] multiplexer_1_out;

  Multiplexer #(.select(2), .width(8), .enable("false")) multiplexer_1 (
    .in0(in_1[7:0]), .in1(in_1[15:8]), .in2(in_1[23:16]), .in3(in_1[31:24]), .out(multiplexer_1_out),
    .sel(in_2));
  Multiplexer #(.width(32), .enable("false")) multiplexer_2 (
    .in0(in_1), .in1({{25{multiplexer_1_out[7]}}, multiplexer_1_out[6:0]}), .out(out_4), .sel(ByteOrWord));
endmodule

module TypeRControl (
  input  [5:0] opcode,
  input  [5:0] funct,
  input  Manual,
  output TypeRInstruction,
  output [14:0] out_5
);

  wire and_1_out, not_1_out, or_1_out, or_2_out, or_3_out;

  and and_1 (and_1_out, TypeRInstruction, not_1_out);
  not not_1 (not_1_out, Manual);
  ROM #(.addrWidth(6), .dataWidth(15)) rom_1 (.addr(funct), .data(out_5), .sel(and_1_out));
  or or_1 (or_1_out, opcode[0], opcode[1], opcode[2]);
  or or_2 (or_2_out, opcode[3], opcode[4], opcode[5]);
  or or_3 (or_3_out, or_1_out, or_2_out);
  not not_2 (TypeRInstruction, or_3_out);

  // Notes on the sheet:
  //   contents of rom_1 (hex, n*v repeats v):
  //   9*0 2a41 16*0 241 5*0 241 0 241 0 241 241 4*0 241
endmodule
